# Fritzing sketch SensorXIAO (saved by Fritzing 1.0.3b)

parts:
  U1 = XIAO ESP32C6 [part_number=" XIAO ESP32C6"]
  C1_100n = Capacitor [package=cap-pth-small2]
  R2 = Resistor [tolerance=±5% power=0.25W resistance=220k package=THT]
  U2 = LIPO-1000mAh [package=lipo-1000]
  R1 = Resistor [tolerance=±5% power=0.25W resistance=220k package=THT]
  U3 = XIAO ESP32C6 [part_number=" XIAO ESP32C6"]
  BME280/BME680 = BME280 Breakout
  Part1 = BME280 Breakout  # not connected
  U4 = XIAO ESP32C6 [part_number=" XIAO ESP32C6"]
  Part2 = Adafruit SGP40

nets:
  N1: U1.D0, C1_100n.1, R2.Pin_0, R1.Pin_1
  N2: U1.GND, R1.Pin_0
  N3: R2.Pin_1, U2.+
  N4: U3.D3, BME280/BME680.3.3V
  N5: U3.D4, BME280/BME680.SDI/SDA
  N6: U3.D5, BME280/BME680.SCK/SCL
  GND: U3.GND, BME280/BME680.GND
  N7: U4.D3, U4.D4, Part2.SDA
  N8: U4.D5, U4.D6, Part2.SCL
  3V3: U4.3V3, Part2.3.3V
  GND_2: U4.GND, Part2.GND

custom parts:
  XIAO ESP32C6: XIAO ESP32C6 is a cost-effective MCU based on Espressif’s ESP32-C6. This compact MCU excels in Matter-compliant smart home applications with its support for various wireless connectivity (2.4GHz Wi-Fi 6, BLE 5.0, Zigbee, and Thread). Designed with the thumb-size footprint and a single-sided mount of the XIAO Series, it's perfect for space-limited projects. Encrypted on the chip, the XIAO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
